# Fritzing sketch board_schematic (saved by Fritzing 0.9.3b)
breadboards: 1

parts:
  Part1 = Arduino Ethernet Shield (Rev3)
  R1 = Resistor [tolerance=±5% resistance=1k package="0402 [SMD]"]
  J1 = Basic Force Sensing Resistor (FSR) [package=THT]
  Part2 = Triple Axis Accelerometer Breakout - ADXL345
  J2 = Basic Force Sensing Resistor (FSR) [package=THT]
  R2 = Resistor [tolerance=±5% resistance=1k package="0402 [SMD]"]

nets:
  N1: Part1.A2, J2.pin_1, R2.Pin_1
  N2: Part1.A4/SDA, Part2.SDA
  N3: Part1.A5/SCL, R1.Pin_1, J1.pin_1, Part2.SCL
  5V: Part1.5V, J1.pin_0, Part2.VCC, J2.pin_0
  GND: Part1.GND, R1.Pin_0, Part2.GND, R2.Pin_0
